# Fritzing sketch LM35_Basic (saved by Fritzing 0.9.3b)
circuit board: 8.46667cm x 5.64444cm
breadboards: 1

parts:
  R1 = Rotary Potentiometer (Small) [maximum_resistance=100kΩ package=THT]
  Part1 = Arduino Uno (Rev3)
  C2 = Electrolytic Capacitor [capacitance=4.7µF voltage=35V package="1010 [SMD, electrolytic]"]
  C3 = Electrolytic Capacitor [capacitance=100µF voltage=35V package="200 mil [THT, electrolytic]"]
  Part2 = songle relay
  JP1 = Header 3 [package=screwterminal-3.5mm-3_lock.007s]

nets:
  N1: R1.leg1, Part1.GND, C2.-, C3.-
  N2: R1.wiper, Part1.A0, C2.+
  N3: R1.leg2, Part1.5V, C3.+
  N4: Part2.NO, JP1.3
  N5: Part2.NC, JP1.1
  N6: Part2.COMMON, JP1.2
